// Digital circuit CU_32bits.dig as structural Verilog
module CU_32bits (
  input  [31:0] Instruction,
  output ImmediateRegister,
  output DMwrEnable,
  output JAL___JALR,
  output [1:0] WBSel,
  output Store,
  output Load,
  output Branch,
  output RegisterFileEnable,
  output SRAI___Sub,
  output [2:0] Function3,
  output [6:0] Function7,
  output [6:0] OpCode
);

  wire Imm_eq, JAL_eq, JALR_eq, Load_eq, or_2_out, R_eq;
  wire [1:0] multiplexer_1_out;
  wire [2:0] deco_32bit_1_function3;

  Deco_32bit deco_32bit_1 (
    .Inst(Instruction), .OpCode(OpCode), .Function3(deco_32bit_1_function3), .Function7(Function7));  // open: Read, RS1, Rs2
  Comparator #(.Bits(7)) R (.a(OpCode), .b(7'b0110011), .eq(R_eq));  // open: gt, lt
  Comparator #(.Bits(7)) Imm (.a(OpCode), .b(7'b0010011), .eq(Imm_eq));  // open: gt, lt
  Comparator #(.Bits(7)) S (.a(OpCode), .b(7'b0100011), .eq(DMwrEnable));  // open: gt, lt
  Comparator #(.Bits(7)) u_Load (.a(OpCode), .b(7'b0000011), .eq(Load_eq));  // open: gt, lt
  Comparator #(.Bits(7)) JAL (.a(OpCode), .b(7'b1101111), .eq(JAL_eq));  // open: gt, lt
  Comparator #(.Bits(7)) JALR (.a(OpCode), .b(7'b1100111), .eq(JALR_eq));  // open: gt, lt
  Comparator #(.Bits(7)) u_Store (.a(OpCode), .b(7'b0100011), .eq(Store));  // open: gt, lt
  Comparator #(.Bits(7)) Load_2 (.a(OpCode), .b(7'b0000011), .eq(Load));  // open: gt, lt
  Comparator #(.Bits(7)) u_Branch (.a(OpCode), .b(7'b1100011), .eq(Branch));  // open: gt, lt
  not not_1 (ImmediateRegister, R_eq);
  or or_1 (JAL___JALR, JAL_eq, JALR_eq);
  or or_2 (or_2_out, Branch, R_eq, Imm_eq);
  Multiplexer #(.Bits(2)) multiplexer_1 (.sel(JAL___JALR), .in_0(2'b00), .in_1(2'b10), .out(multiplexer_1_out));
  Multiplexer #(.Bits(2)) multiplexer_2 (.sel(Load_eq), .in_0(2'b01), .in_1(multiplexer_1_out), .out(WBSel));
  Multiplexer multiplexer_3 (.sel(or_2_out), .in_0(Function7[4]), .in_1(1'b0), .out(SRAI___Sub));
  Multiplexer #(.Bits(3)) multiplexer_4 (.sel(Branch), .in_0(deco_32bit_1_function3), .in_1(3'b000), .out(Function3));
  or or_3 (RegisterFileEnable, R_eq, Imm_eq, JAL___JALR, Load);
endmodule
