// Digital circuit ProcesadorMonociclo_32bits.dig as structural Verilog
module ProcesadorMonociclo_32bits (
  input  Clock,
  input  Reset
);

  wire alu_32bit_1_p5, branch_32bit_1_p5, cu_32bits_1_p3, datamemory_32bits_1_p5, DMwrEn, Function3,
       Function7, immediate_32bits_1_p2, multiplexer_1_out, multiplexer_2_out, pc_32bit_1_p1, pc_32bit_1_p3,
       rf24_32bit_1_p1, rf24_32bit_1_p7, rf24_32bit_1_p8, RFwrEnable;
  wire [4:0] pm24_32bit_1_inst_2, pm24_32bit_1_inst_3, pm24_32bit_1_inst_4;
  wire [31:0] add_1_s, pc_32bit_1_p5, pm24_32bit_1_inst;

  // PC_32bit pc_32bit_1: pin names not known; wires that end beside it: pc_32bit_1_p1, Clock, pc_32bit_1_p3, Reset, pc_32bit_1_p5
  Add #(.Bits(32)) add_1 (.a(32'h4), .b(pc_32bit_1_p5), .s(add_1_s));  // open: c_i, c_o
  PM24_32bit pm24_32bit_1 (
    .Addres(pc_32bit_1_p5),
    .Inst({pm24_32bit_1_inst[31:25], pm24_32bit_1_inst_4, pm24_32bit_1_inst_3, pm24_32bit_1_inst[14:12], pm24_32bit_1_inst_2, pm24_32bit_1_inst[6:0]}));
  // CU_32bits cu_32bits_1: pin names not known; wires that end beside it: {pm24_32bit_1_inst[31:25], pm24_32bit_1_inst_4, pm24_32bit_1_inst_3, pm24_32bit_1_inst[14:12], pm24_32bit_1_inst_2, pm24_32bit_1_inst[6:0]}, DMwrEn, cu_32bits_1_p3, RFwrEnable, Function3, Function7
  // Immediate_32bits immediate_32bits_1: pin names not known; wires that end beside it: {pm24_32bit_1_inst[31:25], pm24_32bit_1_inst_4, pm24_32bit_1_inst_3, pm24_32bit_1_inst[14:12], pm24_32bit_1_inst_2, pm24_32bit_1_inst[6:0]}, immediate_32bits_1_p2
  // RF24_32bit rf24_32bit_1: pin names not known; wires that end beside it: rf24_32bit_1_p1, Clock, RFwrEnable, pm24_32bit_1_inst_2, pm24_32bit_1_inst_3, pm24_32bit_1_inst_4, rf24_32bit_1_p7, rf24_32bit_1_p8
  Multiplexer multiplexer_1 (
    .in_0(pm24_32bit_1_inst[0]), .in_1(rf24_32bit_1_p7), .out(multiplexer_1_out));  // open: sel
  Multiplexer multiplexer_2 (
    .in_0(rf24_32bit_1_p8), .in_1(immediate_32bits_1_p2), .out(multiplexer_2_out));  // open: sel
  // Branch_32bit branch_32bit_1: pin names not known; wires that end beside it: Function3, cu_32bits_1_p3, rf24_32bit_1_p8, rf24_32bit_1_p7, branch_32bit_1_p5, pc_32bit_1_p3
  // ALU_32bit alu_32bit_1: pin names not known; wires that end beside it: multiplexer_1_out, multiplexer_2_out, Function3, Function7, alu_32bit_1_p5
  Multiplexer multiplexer_3 (.sel(branch_32bit_1_p5), .in_0(add_1_s[0]), .in_1(alu_32bit_1_p5), .out(pc_32bit_1_p1));
  // DataMemory_32bits datamemory_32bits_1: pin names not known; wires that end beside it: Clock, DMwrEn, Function3, alu_32bit_1_p5, datamemory_32bits_1_p5
  Multiplexer #(.Selector_Bits(2)) multiplexer_4 (
    .in_0(alu_32bit_1_p5), .in_1(datamemory_32bits_1_p5), .out(rf24_32bit_1_p1));  // open: sel, in_2, in_3
  // Pins of 1 and 32 bits meet at {pm24_32bit_1_inst[31:25], pm24_32bit_1_inst_4, pm24_32bit_1_inst_3, pm24_32bit_1_inst[14:12], pm24_32bit_1_inst_2, pm24_32bit_1_inst[6:0]}
  // Pins of 1 and 32 bits meet at add_1_s
endmodule
